# Fritzing sketch can-i.help (saved by Fritzing 0.9.2b)
breadboards: 1

parts:
  Part1 = Arduino Uno (Rev3)
  LED1 = RGB LED - (4 legs) [package="5 mm [THT]"]
  LCD2 = LCD screen
  R1 = Resistor [tolerance=±5% resistance=1k package="2010 [SMD]"]
  R2 = Resistor [tolerance=±5% resistance=1k package="2010 [SMD]"]
  U3 = Voltage Regulator [package=to220-adj]
  R3 = Resistor [tolerance=±5% resistance=220 package="2010 [SMD]"]
  R4 = Resistor [tolerance=±5% resistance=360 package="2010 [SMD]"]
  0_1uF = Capacitor [package=cap-pth-large]
  0_1uF_2 = Capacitor [package=cap-pth-large]
  ESP8266 = ESP8266 WiFi Module [part_number=ESP-03]

nets:
  N1: Part1.A0, LCD2.RS
  N2: Part1.A1, LCD2.E
  N3: Part1.A2, LCD2.DB4
  N4: Part1.A3, LCD2.DB5
  N5: Part1.A4/SDA, LCD2.DB6
  N6: Part1.A5/SCL, LCD2.DB7
  N7: Part1.D8, ESP8266.RXD
  GND: Part1.GND, LED1.red_cathode, LCD2.VSS, LCD2.R/W, LCD2.LED-, R1.Pin_0, U3.OUT, R4.Pin_1, 0_1uF.2, 0_1uF_2.1, 0_1uF_2.2, ESP8266.GND
  N8: Part1.D4, LED1.blue_cathode
  N9: Part1.D5_PWM, LED1.green_cathode
  N10: Part1.D6_PWM, LED1.common_anode
  N11: Part1.D7, U3.IN, R3.Pin_1, 0_1uF.1, ESP8266.VCC, ESP8266.GPIO_16, ESP8266.CH_PD, ESP8266.TXD
  5V: Part1.5V, LCD2.VDD, R2.Pin_0
  N12: LCD2.V0, R1.Pin_1
  N13: LCD2.LED+, R2.Pin_1
  N14: U3.ADJ, R3.Pin_0, R4.Pin_0

custom parts:
  ESP8266 WiFi Module: Generic WiFi Module based on the ESP8266 with onboard PCB antenna and UART communications
